# Fritzing sketch weatherstation (saved by Fritzing 0.7.11b)
breadboards: 1

parts:
  Arduino3 = Arduino Fio
  RHT3 = Humidity and Temperature Sensor RHT03
  BMP3 = BMP085 Breakout
  R3 = Resistor [tolerance=±5% resistance=220 package=THT]
  R4 = Resistor [tolerance=±5% resistance=680k package=THT]
  R5 = Resistor [tolerance=±5% resistance=100k package=THT]
  R6 = Resistor [tolerance=±5% resistance=330k package=THT]
  R7 = Resistor [tolerance=±5% resistance=100k package=THT]
  J1 = Screw terminal - 2 pins [package=THT]
  J2 = Screw terminal - 2 pins [package=THT]  # not connected

nets:
  N1: Arduino3.A5, BMP3.SCL
  N2: Arduino3.A4, BMP3.SDA
  N3: Arduino3.A1, R4.Pin_1, R7.Pin_0
  N4: Arduino3.A0, R5.Pin_0, R6.Pin_1
  N5: Arduino3.GND, RHT3.GND_2, R5.Pin_1, R7.Pin_1
  N6: Arduino3.D12, RHT3.Data-signal, R3.Pin_0
  N7: RHT3.Vcc, BMP3.3Vo
  N8: R4.Pin_0, J1.pin2
  N9: R6.Pin_0, J1.pin1

custom parts:
  BMP085 Breakout: A breakout for the BMP085 barometric pressure and temperature sensor
